# Fritzing sketch 4.1 (saved by Fritzing 0.9.4)
breadboards: 1

parts:
  Mod2 = Raspberry Pi Pico
  LED1 = RGB LED (com. cathode, rgb) [package="5 mm [THT]"]

nets:
  N1: Mod2.pin_3, Mod2.pin_8, Mod2.pin_13, Mod2.pin_18, Mod2.pin_23, Mod2.pin_28, Mod2.pin_33, Mod2.pin_38, LED1.green_anode
  N2: Mod2.pin_19, LED1.red_anode
  N3: Mod2.pin_20, LED1.common_cathode
  N4: Mod2.pin_21, LED1.blue_anode

custom parts:
  Raspberry Pi Pico: Raspberry Pi Pico. Based around the RP2040 microcontroller the Pico is a low cost microcontroller device bringing Raspberry Pi quality, cost, and easy of use to the microcontroller space. Jan 2021, Split part in to two versions: tht (this one) and SMD. This one will drill holes for a .1 in header in pcb to allow plugging in the module as well as providing pads to solder the module to the top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
