# Fritzing sketch M (saved by Fritzing 0.9.4)
breadboards: 2

parts:
  Mod2 = Raspberry Pi Pico
  LED1 = smd LED [color="Red (633nm)" package="0805 [SMD]"]
  S2 = Momentary Switch 6mm 2pin
  S1 = Momentary Switch 6mm 2pin
  S3 = Momentary Switch 6mm 2pin
  LED5 = smd LED [color="Red (633nm)" package="0805 [SMD]"]
  LED6 = smd LED [color="Red (633nm)" package="0805 [SMD]"]
  M1 = DC Motor
  M2 = DC Motor
  M3 = DC Motor
  VCC1 = 4 x AAA Battery Mount
  Q1 = BD140 [package="TO-126 [THT]"]
  Q2 = BD140 [package="TO-126 [THT]"]
  Q3 = BD140 [package="TO-126 [THT]"]
  TTP223B1 = TTP223B Capacitive Touch Sensor Module

nets:
  N1: Mod2.pin_3, Mod2.pin_8, Mod2.pin_13, Mod2.pin_18, Mod2.pin_23, Mod2.pin_28, Mod2.pin_33, Mod2.pin_38, Mod2.pin_42, LED1.cathode, S2.2, S1.1, S3.1, LED5.cathode, LED6.cathode, M1.pin_2, M2.pin_2, M3.pin_2, VCC1.-, TTP223B1.GND
  N2: Mod2.pin_10, S3.2
  N3: Mod2.pin_15, Q3.emitter
  N4: Mod2.pin_16, Q1.emitter
  N5: Mod2.pin_17, Q2.emitter
  N6: Mod2.pin_19, LED6.anode
  N7: Mod2.pin_20, S2.1
  N8: Mod2.pin_21, S1.2
  N9: Mod2.pin_22, LED5.anode
  N10: Mod2.pin_31, TTP223B1.SIG
  N11: Mod2.pin_32, LED1.anode
  N12: Mod2.pin_36, TTP223B1.VCC
  N13: M1.pin_1, Q2.collector
  N14: M2.pin_1, Q1.collector
  N15: M3.pin_1, Q3.collector
  N16: VCC1.+, Q1.base, Q2.base, Q3.base

custom parts:
  Raspberry Pi Pico: Raspberry Pi Pico. Based around the RP2040 microcontroller the Pico is a low cost microcontroller device bringing Raspberry Pi quality, cost, and easy of use to the microcontroller space. Jan 2021, Split part in to two versions: tht (this one) and SMD. This one will drill holes for a .1 in header in pcb to allow plugging in the module as well as providing pads to solder the module to the top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
  Momentary Switch 6mm 2pin: Momentary Switch 6mm 2 pin Button commonly used for reset or general input.
  BD140: A pnp transistor which can drive a higher load
  TTP223B Capacitive Touch Sensor Module: The TTP223B capacitive touch sensor module uses the TTP223B IC. The appropriate voltage is approximately 2 to 5.5 volts.
