# Fritzing sketch TM.1 (saved by Fritzing 0.9.4)
breadboards: 1

parts:
  Mod2 = Raspberry Pi Pico
  LED1 = smd LED [color="Red (633nm)" package="0805 [SMD]"]
  S2 = Momentary Switch 6mm 2pin
  S1 = Momentary Switch 6mm 2pin
  S3 = Momentary Switch 6mm 2pin
  LED5 = smd LED [color="Red (633nm)" package="0805 [SMD]"]
  LED6 = smd LED [color="Red (633nm)" package="0805 [SMD]"]
  LED7 = smd LED [color="Red (633nm)" package="0805 [SMD]"]
  LED8 = smd LED [color="Red (633nm)" package="0805 [SMD]"]
  LED9 = smd LED [color="Red (633nm)" package="0805 [SMD]"]
  TTP223B1 = TTP223B Capacitive Touch Sensor Module

nets:
  N1: Mod2.pin_3, Mod2.pin_8, Mod2.pin_13, Mod2.pin_18, Mod2.pin_23, Mod2.pin_28, Mod2.pin_33, Mod2.pin_38, Mod2.pin_42, LED1.cathode, S2.2, S1.1, S3.1, LED5.cathode, LED6.cathode, LED7.cathode, LED8.cathode, LED9.cathode, TTP223B1.GND
  N2: Mod2.pin_10, S3.2
  N3: Mod2.pin_15, LED9.anode
  N4: Mod2.pin_16, LED8.anode
  N5: Mod2.pin_17, LED7.anode
  N6: Mod2.pin_19, LED6.anode
  N7: Mod2.pin_20, S2.1
  N8: Mod2.pin_21, S1.2
  N9: Mod2.pin_22, LED5.anode
  N10: Mod2.pin_31, TTP223B1.SIG
  N11: Mod2.pin_32, LED1.anode
  N12: Mod2.pin_36, TTP223B1.VCC

custom parts:
  Raspberry Pi Pico: Raspberry Pi Pico. Based around the RP2040 microcontroller the Pico is a low cost microcontroller device bringing Raspberry Pi quality, cost, and easy of use to the microcontroller space. Jan 2021, Split part in to two versions: tht (this one) and SMD. This one will drill holes for a .1 in header in pcb to allow plugging in the module as well as providing pads to solder the module to the top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
  Momentary Switch 6mm 2pin: Momentary Switch 6mm 2 pin Button commonly used for reset or general input.
  TTP223B Capacitive Touch Sensor Module: The TTP223B capacitive touch sensor module uses the TTP223B IC. The appropriate voltage is approximately 2 to 5.5 volts.
